# Fritzing sketch TicTacToe (saved by Fritzing 0.7.10b)
breadboards: 1

parts:
  Set = Pushbutton [package="[THT]"]
  Next = Pushbutton [package="[THT]"]
  R1 = Resistor [tolerance=±5% resistance=1k package=THT]
  R2 = Resistor [tolerance=±5% resistance=1k package=THT]
  Arduino1 = Arduino
  LCD_128x1 = 128 x 160 Graphic LCD 1.8" [part_number="SainSmart 1.8 SPI LCD"]

nets:
  N1: Set.Pin_1, Set.Pin_2, R1.Pin_1, Arduino1.D10
  N2: Set.Pin_3, Set.Pin_4, Next.Pin_3, Next.Pin_4, Arduino1.+5V, LCD_128x1.1_Vcc
  N3: Next.Pin_1, Next.Pin_2, R2.Pin_0, Arduino1.D11
  N4: R1.Pin_0, R2.Pin_1, Arduino1.GND, LCD_128x1.2_GND
  N5: Arduino1.D8, LCD_128x1.6_RES
  N6: Arduino1.D7, LCD_128x1.5_RS/DC
  N7: Arduino1.D6, LCD_128x1.7_CS
  N8: Arduino1.D5, LCD_128x1.4_SDA
  N9: Arduino1.D4, LCD_128x1.3_SCL
